# Fritzing sketch esquematico (saved by Fritzing 0.9.3b)
breadboards: 1

parts:
  Componente1 = Arduino Uno (Rev3)
  M2 = DC Motor
  L298N1 = L298N DC motor driver
  D1 = Diode [package=diode-1n4001]  # not connected
  M3 = DC Motor
  VCC1 = 4 x AAA Battery Mount
  M6 = DC Motor
  M7 = DC Motor
  L298N3 = L298N DC motor driver
  Componente2 = Bluetooth HC-05 Macho

nets:
  N1: Componente1.D8, L298N3.IN2
  N2: Componente1.D9_PWM, L298N3.IN1
  N3: Componente1.D0/RX, Componente2.TXD
  N4: Componente1.D1/TX, Componente2.RXD
  N5: Componente1.D2, L298N1.IN1
  N6: Componente1.D3_PWM, L298N1.IN2
  N7: Componente1.D4, L298N1.IN3
  N8: Componente1.D5_PWM, L298N1.IN4
  N9: Componente1.D6_PWM, L298N3.IN4
  N10: Componente1.D7, L298N3.IN3
  3V3: Componente1.3V3, Componente2.VCC
  5V: Componente1.5V, L298N1.5V, VCC1.+, L298N3.12V, L298N3.5V
  GND: Componente1.GND, L298N1.12V, L298N1.GND, VCC1.-, L298N3.GND, Componente2.GND
  N11: M2.pin_1, L298N1.OUT2
  N12: M2.pin_2, L298N1.OUT1
  N13: L298N1.OUT3, L298N1.OUT4, M3.pin_1, M3.pin_2
  N14: M6.pin_1, L298N3.OUT2
  N15: M6.pin_2, L298N3.OUT1
  N16: M7.pin_1, L298N3.OUT4
  N17: M7.pin_2, L298N3.OUT3

custom parts:
  L298N DC motor driver: 2x DC motor driver with 78M05 positive voltage regulator (7..35 V) L298N: max 46 V, 2 A Set 5 V Enable jumper to enable 5 V regultor (needed for the L298N) and +5 V output at screw terminal or supply external +5 V at screw terminal Set ENA and/or ENB to +5 V to enable motor permanently or supply ENA and/or ENB with PWM signal IN1 and IN2 set rotation directory for motor A (OUT1/OUT2) IN2 and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
