# Fritzing sketch step_2 (saved by Fritzing 0.9.3b)
breadboards: 1

parts:
  Componente1 = Arduino Uno (Rev3)
  VCC1 = 4 x AAA Battery Mount
  D1 = Diode [package=diode-1n4001]  # not connected
  LED1 = LED - 5mm [color="Yellow (595nm)" package="5 mm [THT]"]
  R1 = Resistor [tolerance=±5% resistance=220 package=THT]

nets:
  N1: Componente1.D13/SCK, LED1.anode
  N2: Componente1.GND, VCC1.-, R1.Pin_0
  N3: LED1.cathode, R1.Pin_1
