# Fritzing sketch step_3 (saved by Fritzing 0.9.3b)
breadboards: 1

parts:
  Componente1 = Arduino Uno (Rev3)
  M2 = DC Motor
  L298N1 = L298N DC motor driver
  VCC1 = 4 x AAA Battery Mount
  D1 = Diode [package=diode-1n4001]  # not connected

nets:
  N1: Componente1.D2, L298N1.IN1
  N2: Componente1.D3_PWM, L298N1.IN2
  GND: Componente1.GND, L298N1.GND, VCC1.-
  N3: M2.pin_1, L298N1.OUT2
  N4: M2.pin_2, L298N1.OUT1
  N5: L298N1.12V, L298N1.5V#7, VCC1.+
  N6: L298N1.5V#9, L298N1.ENA
  N7: L298N1.5V#10, L298N1.ENB

custom parts:
  L298N DC motor driver: 2x DC motor driver with 78M05 positive voltage regulator (7..35 V) L298N: max 46 V, 2 A Set 5 V Enable jumper to enable 5 V regultor (needed for the L298N) and +5 V output at screw terminal or supply external +5 V at screw terminal Set ENA and/or ENB to +5 V to enable motor permanently or supply ENA and/or ENB with PWM signal IN1 and IN2 set rotation directory for motor A (OUT1/OUT2) IN2 and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
