# Fritzing sketch esquematico (saved by Fritzing 0.9.3b)
breadboards: 1

parts:
  Componente1 = Arduino Uno (Rev3)
  M3 = DC Motor
  M6 = DC Motor  # not connected
  M7 = DC Motor
  L298N3 = L298N DC motor driver
  VCC2 = Battery block 9V
  M8 = DC Motor
  VCC3 = Battery block 9V  # not connected
  Componente2 = Bluetooth HC-05 Macho

nets:
  N1: Componente1.D9_PWM, L298N3.IN1
  N2: Componente1.D10_PWM/SS, L298N3.IN2
  N3: Componente1.D11_PWM/MOSI, L298N3.IN3
  N4: Componente1.D12/MISO, L298N3.IN4
  N5: Componente1.D0/RX, Componente2.TXD
  5V: Componente1.5V, Componente2.VCC
  GND: Componente1.GND, Componente2.GND
  N6: M3.pin_1, L298N3.OUT2, M8.pin_1
  N7: M3.pin_2, L298N3.OUT1, M8.pin_2
  N8: M7.pin_1, L298N3.OUT4
  N9: M7.pin_2, L298N3.OUT3
  N10: L298N3.12V, L298N3.5V#7, VCC2.+
  N11: L298N3.GND, VCC2.-
  N12: L298N3.5V#9, L298N3.ENA
  N13: L298N3.5V#10, L298N3.ENB

notes:
  FRONT OF THE CAR

custom parts:
  L298N DC motor driver: 2x DC motor driver with 78M05 positive voltage regulator (7..35 V) L298N: max 46 V, 2 A Set 5 V Enable jumper to enable 5 V regultor (needed for the L298N) and +5 V output at screw terminal or supply external +5 V at screw terminal Set ENA and/or ENB to +5 V to enable motor permanently or supply ENA and/or ENB with PWM signal IN1 and IN2 set rotation directory for motor A (OUT1/OUT2) IN2 and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
